# Fritzing sketch hourglassfzz (saved by Fritzing 0.9.3b)

parts:
  Part1 = Arduino Nano (Rev3.0)
  M1 = MAX7219 8x8 single Led Matrix Module
  A1 = SM5308 battery charger module
  Part2 = Triple Axis Accelerometer Breakout - ADXL335
  BAT1 = LIPO-110mAh [package=lipo-110]
  M2 = MAX7219 8x8 single Led Matrix Module

nets:
  N1: Part1.D4, M1.I-CLK, M1.O-CLK, M2.I-CLK
  N2: Part1.D5, M1.O-DOUT
  N3: Part1.D6, M1.I-CS, M1.O-CS, M2.I-CS
  N4: Part1.GND, A1.Pin_1, A1.Pin_5, BAT1.-
  N5: Part1.5V, A1.Pin_4
  N6: Part1.A2, Part2.YOUT
  N7: Part1.A1, Part2.XOUT
  N8: M1.I-DIN, M2.I-DIN
  N9: M1.I-GND, M1.O-GND, M2.I-GND
  N10: M1.I-VCC, M1.O-VCC, M2.I-VCC
  N11: A1.Pin_2, BAT1.+

custom parts:
  MAX7219 8x8 single Led Matrix Module: Description: MAX7219 8x8 LedMatrix single Red Module Dimensions: 32x32mm Documents:
  SM5308 battery charger module: Charger module for Lipo Battery from Usb, 5v 2a, Sm5308 chip.
